// Digital circuit cpu_2.dig as structural Verilog
module cpu_2 (
);

  wire _74574_1_pin1, _74574_1_pin11;
  wire [31:0] _74574_1_pin19;

  _74574 _74574_1 (
    .pin1(_74574_1_pin1), .pin11(_74574_1_pin11), .pin12(_74574_1_pin19[7]), .pin13(_74574_1_pin19[6]),
    .pin14(_74574_1_pin19[5]), .pin15(_74574_1_pin19[4]), .pin16(_74574_1_pin19[3]),
    .pin17(_74574_1_pin19[2]), .pin18(_74574_1_pin19[1]), .pin19(_74574_1_pin19[0]), .pin20(1'b1));  // open: pin2, pin3, pin4, pin5, pin6, pin7, pin8, pin9, pin10
  _74574 _74574_2 (
    .pin1(_74574_1_pin1), .pin11(_74574_1_pin11), .pin12(_74574_1_pin19[15]), .pin13(_74574_1_pin19[14]),
    .pin14(_74574_1_pin19[13]), .pin15(_74574_1_pin19[12]), .pin16(_74574_1_pin19[11]),
    .pin17(_74574_1_pin19[10]), .pin18(_74574_1_pin19[9]), .pin19(_74574_1_pin19[8]), .pin20(1'b1));  // open: pin2, pin3, pin4, pin5, pin6, pin7, pin8, pin9, pin10
  _74574 _74574_3 (
    .pin1(_74574_1_pin1), .pin11(_74574_1_pin11), .pin12(_74574_1_pin19[23]), .pin13(_74574_1_pin19[22]),
    .pin14(_74574_1_pin19[21]), .pin15(_74574_1_pin19[20]), .pin16(_74574_1_pin19[19]),
    .pin17(_74574_1_pin19[18]), .pin18(_74574_1_pin19[17]), .pin19(_74574_1_pin19[16]), .pin20(1'b1));  // open: pin2, pin3, pin4, pin5, pin6, pin7, pin8, pin9, pin10
  _74574 _74574_4 (
    .pin1(_74574_1_pin1), .pin11(_74574_1_pin11), .pin12(_74574_1_pin19[31]), .pin13(_74574_1_pin19[30]),
    .pin14(_74574_1_pin19[29]), .pin15(_74574_1_pin19[28]), .pin16(_74574_1_pin19[27]),
    .pin17(_74574_1_pin19[26]), .pin18(_74574_1_pin19[25]), .pin19(_74574_1_pin19[24]), .pin20(1'b1));  // open: pin2, pin3, pin4, pin5, pin6, pin7, pin8, pin9, pin10
endmodule
