// Logisim project jpu.circ as structural Verilog: 3 circuits, main circuit main
module main (
);

  wire undriven, undriven_4, undriven_5, undriven_6, undriven_7, undriven_8, undriven_9;
  wire [7:0] pipestage_1_output_1, pipestage_1_output_2, pipestage_1_output_3, pipestage_1_output_4,
       pipestage_2_output_1, pipestage_2_output_2, pipestage_2_output_3, pipestage_2_output_4, ram_1_data,
       ram_2_data, ram_3_data, ram_4_data, undriven_3;
  wire [31:0] reg_idls_1_output_a, reg_idls_1_output_b, undriven_2;

  Decoder #(.select(3)) decoder_1 ();  // open: out0, out1, out2, out3, out4, out5, out6, out7, sel, en
  reg_IDLS reg_idls_1 (
    .Load_value(undriven_2), .Clock(undriven), .Output_A(reg_idls_1_output_a), .Output_B(reg_idls_1_output_b));  // open: Load, Decrement, Increment, Reset, OE_A, OE_B
  reg_IDLS reg_idls_2 (
    .Load_value(undriven_2), .Clock(undriven), .Output_A(reg_idls_1_output_a), .Output_B(reg_idls_1_output_b));  // open: Load, Decrement, Increment, Reset, OE_A, OE_B
  reg_IDLS reg_idls_3 (
    .Load_value(undriven_2), .Clock(undriven), .Output_A(reg_idls_1_output_a), .Output_B(reg_idls_1_output_b));  // open: Load, Decrement, Increment, Reset, OE_A, OE_B
  Decoder #(.select(3)) decoder_2 ();  // open: out0, out1, out2, out3, out4, out5, out6, out7, sel, en
  reg_IDLS reg_idls_4 (
    .Load_value(undriven_2), .Clock(undriven), .Output_A(reg_idls_1_output_a), .Output_B(reg_idls_1_output_b));  // open: Load, Decrement, Increment, Reset, OE_A, OE_B
  reg_IDLS reg_idls_5 (
    .Load_value(undriven_2), .Clock(undriven), .Output_A(reg_idls_1_output_a), .Output_B(reg_idls_1_output_b));  // open: Load, Decrement, Increment, Reset, OE_A, OE_B
  reg_IDLS reg_idls_6 (
    .Load_value(undriven_2), .Clock(undriven), .Output_A(reg_idls_1_output_a), .Output_B(reg_idls_1_output_b));  // open: Load, Decrement, Increment, Reset, OE_A, OE_B
  reg_IDLS reg_idls_7 (
    .Load_value(undriven_2), .Clock(undriven), .Output_A(reg_idls_1_output_a), .Output_B(reg_idls_1_output_b));  // open: Load, Decrement, Increment, Reset, OE_A, OE_B
  reg_IDLS reg_idls_8 (
    .Load_value(undriven_2), .Clock(undriven), .Output_A(reg_idls_1_output_a), .Output_B(reg_idls_1_output_b));  // open: Load, Decrement, Increment, Reset, OE_A, OE_B
  ROM #(.dataWidth(16)) rom_1 (.addr(pipestage_2_output_1));  // open: data, sel
  RAM ram_1 (
    .addr(undriven_3), .data(ram_1_data), .sel(undriven_5), .clk(undriven_9), .ld(undriven_6),
    .clr(undriven_4));
  pipestage pipestage_1 (
    .input_1(pipestage_2_output_1), .input_2(pipestage_2_output_2), .input_3(pipestage_2_output_3),
    .input_4(pipestage_2_output_4), .Clk(undriven_8), .Rst(undriven_7), .output_1(pipestage_1_output_1),
    .output_2(pipestage_1_output_2), .output_3(pipestage_1_output_3), .output_4(pipestage_1_output_4));
  pipestage pipestage_2 (
    .input_1(ram_1_data), .input_2(ram_2_data), .input_3(ram_3_data), .input_4(ram_4_data), .Clk(undriven_8),
    .Rst(undriven_7), .output_1(pipestage_2_output_1), .output_2(pipestage_2_output_2),
    .output_3(pipestage_2_output_3), .output_4(pipestage_2_output_4));
  RAM ram_2 (
    .addr(undriven_3), .data(ram_2_data), .sel(undriven_5), .clk(undriven_9), .ld(undriven_6),
    .clr(undriven_4));
  RAM ram_3 (
    .addr(undriven_3), .data(ram_3_data), .sel(undriven_5), .clk(undriven_9), .ld(undriven_6),
    .clr(undriven_4));
  RAM ram_4 (
    .addr(undriven_3), .data(ram_4_data), .sel(undriven_5), .clk(undriven_9), .ld(undriven_6),
    .clr(undriven_4));
endmodule

module reg_IDLS (
  input  [31:0] Load_value,
  input  Clock,
  input  Reset,
  input  OE_B,
  input  OE_A,
  input  Load,
  input  Decrement,
  input  Increment,
  output [31:0] Output_A,
  output [31:0] Output_B
);

  wire [1:0] priority_encoder_1_out;
  wire [31:0] adder_1_out, multiplexer_1_out, register_1_q, subtractor_1_out;

  Adder #(.width(32)) adder_1 (.a(32'h1), .b(register_1_q), .out(adder_1_out));  // open: cin, cout
  Subtractor #(.width(32)) subtractor_1 (.a(register_1_q), .b(32'h1), .out(subtractor_1_out));  // open: bin, bout
  Multiplexer #(.select(2), .width(32)) multiplexer_1 (
    .in0(Load_value), .in1(subtractor_1_out), .in2(adder_1_out), .out(multiplexer_1_out),
    .sel(priority_encoder_1_out), .en(1'b1));  // open: in3
  Priority_Encoder #(.select(2)) priority_encoder_1 (
    .in0(Load), .in1(Decrement), .in2(Increment), .out(priority_encoder_1_out));  // open: in3, gs, en_out, en_in
  Register #(.width(32)) register_1 (.D(multiplexer_1_out), .Q(register_1_q), .clk(Clock), .clr(Reset));  // open: en
  assign Output_A = OE_A ? register_1_q : 32'bz;  // Controlled_Buffer controlled_buffer_1
  assign Output_B = OE_B ? register_1_q : 32'bz;  // Controlled_Buffer controlled_buffer_2
endmodule

module pipestage (
  input  [7:0] input_1,
  input  [7:0] input_2,
  input  [7:0] input_3,
  input  [7:0] input_4,
  input  Clk,
  input  Rst,
  output [7:0] output_1,
  output [7:0] output_2,
  output [7:0] output_3,
  output [7:0] output_4
);

  Register register_1 (.D(input_1), .Q(output_1), .clk(Clk), .clr(Rst));  // open: en
  Register register_2 (.D(input_2), .Q(output_2), .clk(Clk), .clr(Rst));  // open: en
  Register register_3 (.D(input_3), .Q(output_3), .clk(Clk), .clr(Rst));  // open: en
  Register register_4 (.D(input_4), .Q(output_4), .clk(Clk), .clr(Rst));  // open: en
endmodule
